// Logisim project cpu.circ as structural Verilog
module ALU_Input_Stage (
  input  Zero,
  input  Negate,
  input  [7:0] Input,
  output [7:0] Output
);

  wire not_1_out, not_2_out;
  wire [7:0] controlled_buffer_1_out;

  not not_1 (not_1_out, Zero);
  assign controlled_buffer_1_out = not_1_out ? Input : 8'bz;  // Controlled_Buffer controlled_buffer_1
  assign controlled_buffer_1_out = Zero ? {8{1'b0}} : 8'bz;  // Controlled_Buffer controlled_buffer_2
  not not_2 (not_2_out, Negate);
  assign Output = not_2_out ? controlled_buffer_1_out : 8'bz;  // Controlled_Buffer controlled_buffer_3
  assign Output = Negate ? ~controlled_buffer_1_out : 8'bz;  // Controlled_Inverter controlled_inverter_1
endmodule

module ALU_Output_Stage (
  input  OE,
  input  Inverted_OE,
  input  [7:0] Input,
  output [7:0] Output
);

  assign Output = OE ? Input : 8'bz;  // Controlled_Buffer controlled_buffer_1
  assign Output = Inverted_OE ? ~Input : 8'bz;  // Controlled_Inverter controlled_inverter_1
endmodule

module ALU_Operation_Stage (
  input  Carry_In,
  input  [1:0] Carry_Select,
  input  [1:0] Operation_Select,
  input  [7:0] Left_Input,
  input  [7:0] Right_Input,
  output [7:0] Output,
  output Carry_Out,
  output Negative_Out,
  output Zero_Out
);

  wire adder_1_cout, decoder_1_out0, decoder_1_out1, decoder_1_out2, decoder_1_out3, multiplexer_1_out,
       right_shifter_1_carry_in_2;
  wire [7:0] adder_1_out, and_1_out, right_shifter_1_output, xor_1_out;

  Adder adder_1 (.a(Left_Input), .b(Right_Input), .out(adder_1_out), .cin(multiplexer_1_out), .cout(adder_1_cout));
  assign and_1_out = Left_Input & Right_Input;  // AND_Gate and_1, 8 bits wide
  assign xor_1_out = Left_Input ^ Right_Input;  // XOR_Gate xor_1, 8 bits wide
  Right_Shifter right_shifter_1 (
    .Input(Left_Input), .Output(right_shifter_1_output), .Carry_In(multiplexer_1_out),
    .Carry_In_2(right_shifter_1_carry_in_2));
  Multiplexer #(.select(2), .enable("false")) multiplexer_1 (
    .in0(1'b0), .in1(1'b1), .in2(Carry_In), .out(multiplexer_1_out), .sel(Carry_Select));  // open: in3
  Multiplexer #(.select(2), .enable("false")) multiplexer_2 (
    .in0(adder_1_cout), .in1(1'b0), .in2(1'b0), .in3(right_shifter_1_carry_in_2), .out(Carry_Out),
    .sel(Operation_Select));
  assign {Negative_Out, Output[6:0]} = decoder_1_out0 ? adder_1_out : 8'bz;  // Controlled_Buffer controlled_buffer_1
  assign {Negative_Out, Output[6:0]} = decoder_1_out1 ? and_1_out : 8'bz;  // Controlled_Buffer controlled_buffer_2
  Decoder #(.select(2), .disabled(0), .enable("false")) decoder_1 (
    .out0(decoder_1_out0), .out1(decoder_1_out1), .out2(decoder_1_out2), .out3(decoder_1_out3),
    .sel(Operation_Select));
  assign {Negative_Out, Output[6:0]} = decoder_1_out2 ? xor_1_out : 8'bz;  // Controlled_Buffer controlled_buffer_3
  assign {Negative_Out, Output[6:0]} = decoder_1_out3 ? right_shifter_1_output : 8'bz;  // Controlled_Buffer controlled_buffer_4
  nor nor_1 (Zero_Out, Negative_Out, Output[6], Output[5], Output[4], Output[3], Output[2], Output[1], Output[0]);

  assign Output[7] = Negative_Out;
endmodule

module Right_Shifter (
  input  Carry_In,
  input  [7:0] Input,
  output [7:0] Output,
  output Carry_In_2
);


  assign Carry_In_2 = Input[0];
  assign Output = {Carry_In, Input[7:1]};
endmodule

module ALU (
  input  Zero_Left,
  input  Negate_Left,
  input  Zero_Right,
  input  Negate_Right,
  input  Carry_In,
  input  [1:0] Carry_Select,
  input  [1:0] Operation_Select,
  input  OE,
  input  Inverted_OE,
  input  [7:0] Left_Input,
  input  [7:0] Right_Input,
  output [7:0] Output,
  output Carry_Out,
  output Negative_Out,
  output Zero_Out
);

  wire [7:0] Left_Input_Stage_output, Operation_Stage_output, Right_Input_Stage_output;

  ALU_Input_Stage Left_Input_Stage (
    .Input(Left_Input), .Output(Left_Input_Stage_output), .Zero(Zero_Left), .Negate(Negate_Left));
  ALU_Input_Stage Right_Input_Stage (
    .Input(Right_Input), .Output(Right_Input_Stage_output), .Zero(Zero_Right), .Negate(Negate_Right));
  ALU_Operation_Stage Operation_Stage (
    .Left_Input(Left_Input_Stage_output), .Right_Input(Right_Input_Stage_output),
    .Output(Operation_Stage_output), .Carry_In(Carry_In), .Carry_Select(Carry_Select),
    .Operation_Select(Operation_Select), .Carry_Out(Carry_Out), .Negative_Out(Negative_Out),
    .Zero_Out(Zero_Out));
  ALU_Output_Stage Output_Stage (.Input(Operation_Stage_output), .Output(Output), .OE(OE), .Inverted_OE(Inverted_OE));
endmodule

module CPU (
  input  Clock,
  input  Reset,
  output R_W,
  output [7:0] Data,
  output [15:0] Address
);

  wire nor_1_out, undriven, undriven_2;
  wire [7:0] alu_1_output, registers_1_left_output, registers_1_right_output;

  Registers registers_1 (
    .Data_In(alu_1_output), .Left_Output(registers_1_left_output), .Right_Output(registers_1_right_output),
    .Clock(Clock), .Reset(Reset), .Address_Output(Address));  // open: Register_To_Write, Left_Operand_Source, Right_Operand_Source, PC_Op_Select
  ALU alu_1 (
    .Left_Input(registers_1_left_output), .Right_Input(registers_1_right_output), .Output(alu_1_output),
    .OE(undriven_2), .Inverted_OE(undriven));  // open: Zero_Left, Negate_Left, Zero_Right, Negate_Right, Carry_In, Carry_Select, Operation_Select, Carry_Out, Negative_Out, Zero_Out
  assign alu_1_output = nor_1_out ? Data : 8'bz;  // Controlled_Buffer controlled_buffer_1
  nor nor_1 (nor_1_out, undriven_2, undriven, R_W);
  assign Data = R_W ? alu_1_output : 8'bz;  // Controlled_Buffer controlled_buffer_2

  // Notes on the sheet:
  //   Data Bus
  //   Left Bus
  //   Right Bus
  //   R/W line goes to our future control logic
endmodule

module Registers (
  input  [2:0] Register_To_Write,
  input  [2:0] Left_Operand_Source,
  input  [1:0] Right_Operand_Source,
  input  [7:0] Data_In,
  input  [1:0] PC_Op_Select,
  input  Clock,
  input  Reset,
  output [7:0] Left_Output,
  output [7:0] Right_Output,
  output [15:0] Address_Output
);

  wire decoder_1_out1, decoder_1_out2, decoder_1_out3, decoder_1_out6, decoder_1_out7, decoder_2_out0,
       decoder_2_out1, decoder_2_out2, decoder_2_out3, decoder_2_out4, decoder_3_out0, decoder_3_out1,
       decoder_3_out2;
  wire [7:0] A_q, program_counter_1_high_output, program_counter_1_low_output, X_q, Y_q;

  Decoder #(.select(3), .disabled(0), .enable("false")) decoder_1 (
    .out1(decoder_1_out1), .out2(decoder_1_out2), .out3(decoder_1_out3), .out6(decoder_1_out6),
    .out7(decoder_1_out7), .sel(Register_To_Write));  // open: out0, out4, out5
  Register A (.D(Data_In), .en(decoder_1_out1), .Q(A_q), .clk(Clock), .clr(Reset));
  Register X (.D(Data_In), .en(decoder_1_out2), .Q(X_q), .clk(Clock), .clr(Reset));
  Register Y (.D(Data_In), .en(decoder_1_out3), .Q(Y_q), .clk(Clock), .clr(Reset));
  Program_Counter program_counter_1 (
    .Low_Output(program_counter_1_low_output), .High_Output(program_counter_1_high_output),
    .Operation_Select(PC_Op_Select), .Clock(Clock), .Reset(Reset));  // open: Data_In
  Register ADL (.D(Data_In), .en(decoder_1_out6), .Q(Address_Output[7:0]), .clk(Clock), .clr(Reset));
  Register ADH (.D(Data_In), .en(decoder_1_out7), .Q(Address_Output[15:8]), .clk(Clock), .clr(Reset));
  Decoder #(.select(3), .disabled(0), .enable("false")) decoder_2 (
    .out0(decoder_2_out0), .out1(decoder_2_out1), .out2(decoder_2_out2), .out3(decoder_2_out3),
    .out4(decoder_2_out4), .sel(Left_Operand_Source));  // open: out5, out6, out7
  assign Left_Output = decoder_2_out0 ? A_q : 8'bz;  // Controlled_Buffer controlled_buffer_1
  assign Left_Output = decoder_2_out1 ? X_q : 8'bz;  // Controlled_Buffer controlled_buffer_2
  assign Left_Output = decoder_2_out2 ? Y_q : 8'bz;  // Controlled_Buffer controlled_buffer_3
  assign Left_Output = decoder_2_out3 ? program_counter_1_low_output : 8'bz;  // Controlled_Buffer controlled_buffer_4
  assign Left_Output = decoder_2_out4 ? program_counter_1_high_output : 8'bz;  // Controlled_Buffer controlled_buffer_5
  Decoder #(.select(2), .disabled(0), .enable("false")) decoder_3 (
    .out0(decoder_3_out0), .out1(decoder_3_out1), .out2(decoder_3_out2), .sel(Right_Operand_Source));  // open: out3
  assign Right_Output = decoder_3_out0 ? A_q : 8'bz;  // Controlled_Buffer controlled_buffer_6
  assign Right_Output = decoder_3_out1 ? X_q : 8'bz;  // Controlled_Buffer controlled_buffer_7
  assign Right_Output = decoder_3_out2 ? Y_q : 8'bz;  // Controlled_Buffer controlled_buffer_8
endmodule

// PC
module Program_Counter (
  input  [1:0] Operation_Select,
  input  [7:0] Data_In,
  input  Clock,
  input  Reset,
  output [7:0] Low_Output,
  output [7:0] High_Output
);

  wire and_1_out, counter_1_carry, decoder_1_out1, decoder_1_out2, decoder_1_out3;

  Decoder #(.select(2), .disabled(0), .enable("false")) decoder_1 (
    .out1(decoder_1_out1), .out2(decoder_1_out2), .out3(decoder_1_out3), .sel(Operation_Select));  // open: out0
  and and_1 (and_1_out, decoder_1_out1, counter_1_carry);
  Counter counter_1 (
    .load(decoder_1_out2), .D(Data_In), .count(decoder_1_out1), .Q(Low_Output), .carry(counter_1_carry),
    .clk(Clock), .clr(Reset));
  Counter counter_2 (
    .load(decoder_1_out3), .D(Data_In), .count(and_1_out), .Q(High_Output), .clk(Clock), .clr(Reset));  // open: carry

  // Notes on the sheet:
  //   00 - No op
  //   01 - Increment
  //   10 - Load Low Byte
  //   11 - Load High Byte
endmodule
